// Logisim project BullsAndCows.circ as structural Verilog: 1 circuit, main circuit main
module main (
);

  wire _0_out, _1_out, _2_out, _3_out, _4_out, _5_out, _6_out, _7_out, _8_out, _9_out, button_2_out,
       button_out, Clock, dead, decoder_1_out0, decoder_1_out1, decoder_1_out2, decoder_1_out3, enter,
       invalid, match;
  wire [1:0] digit_selector_digit_place;
  wire [2:0] state, win_lives_memory_with_samedigit_detector_1_lives;
  wire [3:0] bit_extender_1_out, bulls_1_p7, cows_1_p9, D0, D1, D2, D3, I0, I1, I2, I3, S0, S1, S2, S3, T0,
       T1, T2, T3, win_lives_memory_with_samedigit_detector_1_wins;

  Clock clock_1 (.out(Clock));
  Button _1 (.out(_1_out));
  Button _2 (.out(_2_out));
  Button _5 (.out(_5_out));
  Button _4 (.out(_4_out));
  Button _8 (.out(_8_out));
  Button _7 (.out(_7_out));
  Button _0 (.out(_0_out));
  Button button (.out(button_out));
  Button u_Enter (.out(enter));
  Button _3 (.out(_3_out));
  Button _6 (.out(_6_out));
  Button _9 (.out(_9_out));
  Button button_2 (.out(button_2_out));
  digit_selector digit_selector (
    .L(button_out), .R(button_2_out), .clock(Clock), .state(state), .Digit_Place(digit_selector_digit_place));
  digit_input number_input (
    ._0(_0_out), ._1(_1_out), ._2(_2_out), ._3(_3_out), ._4(_4_out), ._5(_5_out), ._6(_6_out), ._7(_7_out),
    ._8(_8_out), ._9(_9_out), .clock(Clock), .in_12(digit_selector_digit_place), .State(state), .I0(I0),
    .I1(I1), .I2(I2), .I3(I3));
  Hex_Digit_Display hex_digit_display_1 (.value(win_lives_memory_with_samedigit_detector_1_wins));  // open: dp
  win_lives_memory_with_samedigit_detector win_lives_memory_with_samedigit_detector_1 (
    .match(match), .error(invalid), .state(state), .clock(Clock),
    .wins(win_lives_memory_with_samedigit_detector_1_wins),
    .lives(win_lives_memory_with_samedigit_detector_1_lives));
  Hex_Digit_Display hex_digit_display_2 (.value(bit_extender_1_out));  // open: dp
  assign bit_extender_1_out = {{1{1'b0}}, win_lives_memory_with_samedigit_detector_1_lives};  // Bit_Extender bit_extender_1
  and and_1 (dead, win_lives_memory_with_samedigit_detector_1_lives[0], ~win_lives_memory_with_samedigit_detector_1_lives[1], ~win_lives_memory_with_samedigit_detector_1_lives[2]);  // AND_Gate
  store_memory_with_samedigit__detector setup_digits (
    .I0(I0), .I1(I1), .I2(I2), .I3(I3), .Enter(enter), .Error(invalid), .state(state), .clock(Clock),
    .s0(S0), .s1(S1), .s2(S2), .s3(S3));
  store_memory_with_samedigit_detector_trystage try_digits (
    .I0(I0), .I1(I1), .I2(I2), .I3(I3), .Enter(enter), .Error(invalid), .state(state), .clock(Clock),
    .s0(T0), .s1(T1), .s2(T2), .s3(T3));
  // Probe on state
  Circuit_Controller_w__Error_Check circuit_controller_w_error_check_1 (
    .error(invalid), .zerolives(dead), .win(match), .enter(enter), .Clock(Clock), .Output(state));
  Decoder #(.select(2)) decoder_1 (
    .out0(decoder_1_out0), .out1(decoder_1_out1), .out2(decoder_1_out2), .out3(decoder_1_out3),
    .sel(digit_selector_digit_place));  // open: en
  LED led_1 (.in(decoder_1_out3));
  Hex_Digit_Display hex_digit_display_3 (.value(D3));  // open: dp
  LED led_2 (.in(decoder_1_out2));
  LED led_3 (.in(decoder_1_out1));
  Hex_Digit_Display hex_digit_display_4 (.value(D2));  // open: dp
  Hex_Digit_Display hex_digit_display_5 (.value(D1));  // open: dp
  LED led_4 (.in(decoder_1_out0));
  Hex_Digit_Display hex_digit_display_6 (.value(D0));  // open: dp
  digit_display digit_display_picker (
    .I0(I0), .I1(I1), .I2(I2), .I3(I3), .S0(S0), .S1(S1), .S2(S2), .S3(S3), .state(state), .D0(D0), .D1(D1),
    .D2(D2), .D3(D3));
  Hex_Digit_Display hex_digit_display_7 (.value(S2));  // open: dp
  Hex_Digit_Display hex_digit_display_8 (.value(S3));  // open: dp
  // same_digit same_digit_1: pin names not known; wires that end beside it: I0, I1, I2, I3, T0, T1, invalid
  // bulls bulls_1: pin names not known; wires that end beside it: T2, T3, S0, S1, S2, S3, bulls_1_p7, match
  // cows cows_1: pin names not known; wires that end beside it: T0, T1, T2, T3, S0, S1, S2, S3, cows_1_p9
  Hex_Digit_Display hex_digit_display_9 (.value(S1));  // open: dp
  Hex_Digit_Display hex_digit_display_10 (.value(S0));  // open: dp
  Hex_Digit_Display hex_digit_display_11 (.value(bulls_1_p7));  // open: dp
  Hex_Digit_Display hex_digit_display_12 (.value(cows_1_p9));  // open: dp

  // Notes on the sheet:
  //   Inputs
  //   Wins
  //   Lives
  //   Input DisplayDigits
  //   Saved Setup Digits
  //   Bulls
  //   Cows
endmodule
